# Fritzing sketch LoVid-ReactionBubble-IR-BeamBreakReceiver (saved by Fritzing 0.9.1b)

parts:
  Part1 = Pro Trinket 3.3V
  NRF24L1 = NRF24L01

nets:
  GND: Part1.GND, NRF24L1.GND
  +3V3: Part1.+3V3, NRF24L1.VCC
  N1: Part1.D9, NRF24L1.CE
  N2: Part1.D10, NRF24L1.CSN
  N3: Part1.D11, NRF24L1.MOSI
  N4: Part1.D12, NRF24L1.MISO
  N5: Part1.D13, NRF24L1.SCK

custom parts:
  Pro Trinket 3.3V: The Pro Trinket 3.3V is like an Arduino Pro Mini with more pins and USB included. However, it uses 3V logic and 12MHz clock which means it's good when you want a lower-power and lower-voltage setup. Built with the common core Arduino chip, the ATmega328p, it has 18 GPIO, 2 extra analog inputs, 28K of flash, and 2K of RAM. It has onboard USB bootloading support with Optiboot support, so you can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
  NRF24L01: NRF24L01 module
